# Fritzing sketch Raspi3 (saved by Fritzing 0.9.3b)

parts:
  Squix1 = OLED 0.96" 128x64 I2C SSD1306
  Raspberry_Pi_1 = Raspberry Pi 3 [part_number=RPI-3-V1.2]
  LCD2004-I2C1 = LCD2004-I2C
  S1 = Momentary Switch [package=ksa_sealed_tac_switch]
  S2 = Momentary Switch [package=ksa_sealed_tac_switch]
  S3 = Momentary Switch [package=ksa_sealed_tac_switch]
  S4 = Momentary Switch [package=ksa_sealed_tac_switch]

nets:
  VCC: Squix1.VCC, Raspberry_Pi_1.3v3
  GND: Squix1.GND, LCD2004-I2C1.GND
  N1: Squix1.SCL, Raspberry_Pi_1.GPIO3
  N2: Squix1.SCA, Raspberry_Pi_1.GPIO2
  N3: Raspberry_Pi_1.GPIO17, S4.3
  N4: Raspberry_Pi_1.GPIO27, S1.3
  N5: Raspberry_Pi_1.GPIO22, Raspberry_Pi_1.GPIO9, S3.3
  N6: Raspberry_Pi_1.GPIO23, S2.3
  N7: Raspberry_Pi_1.GND, S1.4
  5V: Raspberry_Pi_1.5V, LCD2004-I2C1.VCC

notes:
  station - / + vol - / +

custom parts:
  LCD2004-I2C: A standard character display with 4x20 characters. Comes in many colors with LCM2004 IIC attached.
