# Fritzing sketch RaspiZero (saved by Fritzing 0.9.4)
breadboards: 1

parts:
  MCU1 = Raspberry Pi Zero
  R1 = Resistor [tolerance=±5% resistance=82 package=THT]
  C1 = Ceramic Capacitor [capacitance=100nF package="100 mil [THT, multilayer]"]
  R2 = Resistor [tolerance=±5% resistance=82 package=THT]
  C2 = Ceramic Capacitor [capacitance=100nF package="100 mil [THT, multilayer]"]
  R3 = Resistor [tolerance=±5% resistance=1k package=THT]
  R4 = Resistor [tolerance=±5% resistance=1k package=THT]
  C3 = Electrolytic Capacitor [capacitance=10µF package="100 mil [THT, electrolytic]"]
  C4 = Electrolytic Capacitor [capacitance=10µF package="100 mil [THT, electrolytic]"]
  Bauteil1 = Audio Jack Breakout

nets:
  N1: MCU1.pin_6, MCU1.pin_39, R1.Pin_0, C1.0, R2.Pin_0, C2.1, Bauteil1.GND
  N2: MCU1.pin_12, R4.Pin_1
  N3: MCU1.pin_33, R3.Pin_1
  N4: R1.Pin_1, C1.1, R3.Pin_0, C3.-
  N5: R2.Pin_1, C2.0, R4.Pin_0, C4.+
  N6: C3.+, Bauteil1.TIP
  N7: C4.-, Bauteil1.RING
